// Logisim project karine_cpu_simulation_v1.circ as structural Verilog: 12 circuits, main circuit main
module main (
  input  in_1
);

  wire clock_1_out, cpu_1_ram_load, cpu_1_vram_load;
  wire [15:0] cpu_1_addr_ram, cpu_1_addr_vram, cpu_1_nxt_instrc, cpu_1_out_bus, ram_1_dout, ram_2_dout;
  wire [23:0] rom_1_data;

  Clock clock_1 (.out(clock_1_out));
  RAM #(.addrWidth(16), .dataWidth(16)) ram_1 (
    .addr(cpu_1_addr_ram), .we(cpu_1_ram_load), .oe(1'b1), .clk(clock_1_out), .din(cpu_1_out_bus),
    .dout(ram_1_dout));
  CPU cpu_1 (
    .INSTRC(rom_1_data), .CLK(clock_1_out), .VRAM_IN(ram_1_dout), .RAM_IN(ram_2_dout), .RESET(in_1),
    .OUT_BUS(cpu_1_out_bus), .RAM_LOAD(cpu_1_ram_load), .VRAM_LOAD(cpu_1_vram_load),
    .NXT_INSTRC(cpu_1_nxt_instrc), .ADDR_RAM(cpu_1_addr_ram), .ADDR_VRAM(cpu_1_addr_vram));
  RAM #(.addrWidth(16), .dataWidth(16)) ram_2 (
    .addr(cpu_1_addr_vram), .we(cpu_1_vram_load), .oe(1'b1), .clk(clock_1_out), .din(cpu_1_out_bus),
    .dout(ram_2_dout));
  ROM #(.addrWidth(16), .dataWidth(24)) rom_1 (.addr(cpu_1_nxt_instrc), .data(rom_1_data));

  // Notes on the sheet:
  //   contents of rom_1 (hex, n*v repeats v):
  //   400050 480078 500000 882000 210000 f00000 10*0 a02000
endmodule

module registrador (
  input  CLK,
  input  LOAD,
  input  [15:0] IN16,
  output [15:0] OUT16
);

  binary_cell D0 (.CELL_IN(IN16[0]), .LOAD(LOAD), .CLK(CLK), .CELL_OUT(OUT16[0]));
  binary_cell D1 (.CELL_IN(IN16[1]), .LOAD(LOAD), .CLK(CLK), .CELL_OUT(OUT16[1]));
  binary_cell D2 (.CELL_IN(IN16[2]), .LOAD(LOAD), .CLK(CLK), .CELL_OUT(OUT16[2]));
  binary_cell D3 (.CELL_IN(IN16[3]), .LOAD(LOAD), .CLK(CLK), .CELL_OUT(OUT16[3]));
  binary_cell D4 (.CELL_IN(IN16[4]), .LOAD(LOAD), .CLK(CLK), .CELL_OUT(OUT16[4]));
  binary_cell D5 (.CELL_IN(IN16[5]), .LOAD(LOAD), .CLK(CLK), .CELL_OUT(OUT16[5]));
  binary_cell D6 (.CELL_IN(IN16[6]), .LOAD(LOAD), .CLK(CLK), .CELL_OUT(OUT16[6]));
  binary_cell D7 (.CELL_IN(IN16[7]), .LOAD(LOAD), .CLK(CLK), .CELL_OUT(OUT16[7]));
  binary_cell D8 (.CELL_IN(IN16[7]), .LOAD(LOAD), .CLK(CLK), .CELL_OUT(OUT16[8]));
  binary_cell D9 (.CELL_IN(IN16[8]), .LOAD(LOAD), .CLK(CLK), .CELL_OUT(OUT16[9]));
  binary_cell D10 (.CELL_IN(IN16[9]), .LOAD(LOAD), .CLK(CLK), .CELL_OUT(OUT16[10]));
  binary_cell D11 (.CELL_IN(IN16[11]), .LOAD(LOAD), .CLK(CLK), .CELL_OUT(OUT16[11]));
  binary_cell D12 (.CELL_IN(IN16[12]), .LOAD(LOAD), .CLK(CLK), .CELL_OUT(OUT16[12]));
  binary_cell D13 (.CELL_IN(IN16[13]), .LOAD(LOAD), .CLK(CLK), .CELL_OUT(OUT16[13]));
  binary_cell D14 (.CELL_IN(IN16[14]), .LOAD(LOAD), .CLK(CLK), .CELL_OUT(OUT16[14]));
  binary_cell D15 (.CELL_IN(IN16[15]), .LOAD(LOAD), .CLK(CLK), .CELL_OUT(OUT16[15]));

  // Other names for the same wires on the sheet: IN0 = IN16[0]; IN1 = IN16[1]; IN2 = IN16[2]; IN3 = IN16[3];
  //   IN4 = IN16[4]; IN5 = IN16[5]; IN6 = IN16[6]; IN7 = IN16[7]; IN8 = IN16[8]; IN9 = IN16[9]; IN10 = IN16[10];
  //   IN11 = IN16[11]; IN12 = IN16[12]; IN13 = IN16[13]; IN14 = IN16[14]; IN15 = IN16[15]; D8 = OUT16[8];
  //   D9 = OUT16[9]; D10 = OUT16[10]; D11 = OUT16[11]; D12 = OUT16[12]; D13 = OUT16[13]; D14 = OUT16[14];
  //   D15 = OUT16[15]
endmodule

module binary_cell (
  input  CELL_IN,
  input  LOAD,
  input  CLK,
  output CELL_OUT
);

  wire multiplexer_1_out;

  D_Flip_Flop d_ff_1 (.D(multiplexer_1_out), .clk(CLK), .Q(CELL_OUT));  // open: Qn, preset, reset
  Multiplexer multiplexer_1 (.in0(CELL_OUT), .in1(CELL_IN), .out(multiplexer_1_out), .sel(LOAD));
endmodule

module CPU_Memory_Unit (
  input  CLK,
  input  [15:0] VALUE,
  input  [2:0] ORIGIN_REG_CODE,
  input  LOAD_IMM,
  input  [15:0] RAM_IN,
  input  [2:0] DEST_REG_CODE,
  input  [15:0] VRAM_IN,
  input  [15:0] ALU_OUT,
  output [15:0] L_REG1_OUT,
  output [15:0] L_REG2_OUT,
  output [15:0] ADDR2_OUT,
  output [15:0] OUT_BUS,
  output [15:0] ADDR01_OUT,
  output LOAD_ViREG1,
  output LOAD_ViREG2
);

  wire demultiplexer_1_out0, demultiplexer_1_out1, demultiplexer_1_out2, demultiplexer_1_out3;
  wire [15:0] multiplexer_1_out, multiplexer_2_out, multiplexer_3_out, multiplexer_4_out;

  Multiplexer #(.width(16)) multiplexer_1 (.in0(OUT_BUS), .in1(VALUE), .out(multiplexer_1_out), .sel(LOAD_IMM));
  Multiplexer #(.width(16)) multiplexer_2 (.in0(OUT_BUS), .in1(VALUE), .out(multiplexer_2_out), .sel(LOAD_IMM));
  Multiplexer #(.width(16)) multiplexer_3 (.in0(OUT_BUS), .in1(VALUE), .out(multiplexer_3_out), .sel(LOAD_IMM));
  Multiplexer #(.width(16)) multiplexer_4 (.in0(OUT_BUS), .in1(VALUE), .out(multiplexer_4_out), .sel(LOAD_IMM));
  Demultiplexer #(.select(3)) demultiplexer_1 (
    .out0(demultiplexer_1_out0), .out1(demultiplexer_1_out1), .out2(demultiplexer_1_out2),
    .out3(demultiplexer_1_out3), .out4(LOAD_ViREG1), .out5(LOAD_ViREG2), .in(1'b1), .sel(DEST_REG_CODE));  // open: out6, out7
  registrador L_REG1 (.CLK(CLK), .LOAD(demultiplexer_1_out0), .IN16(multiplexer_1_out), .OUT16(L_REG1_OUT));
  registrador LREG2 (.CLK(CLK), .LOAD(demultiplexer_1_out1), .IN16(multiplexer_2_out), .OUT16(L_REG2_OUT));
  registrador ADDR_REG1 (.CLK(CLK), .LOAD(demultiplexer_1_out2), .IN16(multiplexer_3_out), .OUT16(ADDR2_OUT));
  registrador ADDR_REG2 (.CLK(CLK), .LOAD(demultiplexer_1_out3), .IN16(multiplexer_4_out), .OUT16(ADDR01_OUT));
  Multiplexer #(.select(3), .width(16)) multiplexer_5 (
    .in0(L_REG1_OUT), .in1(L_REG2_OUT), .in2(ADDR2_OUT), .in3(ADDR01_OUT), .in4(RAM_IN), .in5(VRAM_IN),
    .in6(ALU_OUT), .out(OUT_BUS), .sel(ORIGIN_REG_CODE));  // open: in7
endmodule

module Control_Unit (
  input  [23:0] INSTRUCTION,
  output LOAD_IMM,
  output [2:0] ORGIN_CD,
  output [2:0] DST_CD,
  output [15:0] VALUE,
  output [3:0] ALU_OP_CD,
  output [2:0] Y_OP_CD,
  output [2:0] X_OP_CD,
  output [15:0] INSTRC_LN,
  output [1:0] JMP_CD,
  output alu_buffer
);

  wire [3:0] JMP_INSTRC;
  wire [21:0] CMP_INSTRC, LD_INSTRC, SWP_INSTRC;

  Demultiplexer #(.select(2), .width(22)) demultiplexer_1 (
    .out0(SWP_INSTRC), .out1({LD_INSTRC[21:19], VALUE, LD_INSTRC[2:0]}),
    .out2({CMP_INSTRC[21:19], X_OP_CD, Y_OP_CD, ALU_OP_CD, CMP_INSTRC[8:0]}),
    .out3({JMP_CD, INSTRC_LN, JMP_INSTRC}), .in(INSTRUCTION[21:0]), .sel(INSTRUCTION[23:22]));
  and and_1 (LOAD_IMM, INSTRUCTION[22], ~INSTRUCTION[23]);  // AND_Gate
  assign DST_CD = SWP_INSTRC[21:19] | LD_INSTRC[21:19] | CMP_INSTRC[21:19];  // OR_Gate or_1, 3 bits wide
  and and_2 (alu_buffer, ~INSTRUCTION[22], INSTRUCTION[23]);  // AND_Gate
  Multiplexer #(.width(3)) multiplexer_1 (.in0(SWP_INSTRC[18:16]), .in1(3'b110), .out(ORGIN_CD), .sel(alu_buffer));
  Adder adder_1 ();  // open: a, b, out, cin, cout

  // Other names for the same wires on the sheet: CMP_INSTRC[18:9] = {X_OP_CD, Y_OP_CD, ALU_OP_CD};
  //   JMP_INSTRC[21:4] = {JMP_CD, INSTRC_LN}; load_buffer = alu_buffer; LD_INSTRC[18:3] = VALUE

  // Notes on the sheet:
  //   ALU_OP_CODE
  //   Y_CODE
  //   X_CODE
  //   JUMP CODE
  //   ORIGIN CODE
  //   DESTINATION CODE
  //   VALUE
  //   DESTINATION CODE
  //   DESTINATION CODE
  //   INSTRUCTION ADDRESS
  //   selects either the ALU or the Origin to laod into the internal BUS of the Memory unit
endmodule

module ALU (
  input  [3:0] ALU_OP_CODE,
  input  [15:0] X,
  input  [15:0] Y,
  output [15:0] ALU_OUTPUT,
  output Z_FLAG,
  output N_FLAG
);

  wire alu_decoder_1_nx, alu_decoder_1_ny, alu_decoder_1_zx, alu_decoder_1_zy, carry_in;
  wire [15:0] adder_1_out, adder_2_out, and_1_out, multiplexer_1_out, not_1_out, not_2_out, not_3_out,
       or_1_out, X_COMPLEMENT_neg_out, Y_COMPLEMENT_neg_out, ZERO_X_zero_out, ZERO_Y_zero_out;

  ALU_DECODER alu_decoder_1 (
    .ALU_F(ALU_OP_CODE[2:0]), .carry_in(carry_in), .nx(alu_decoder_1_nx), .ny(alu_decoder_1_ny),
    .zx(alu_decoder_1_zx), .zy(alu_decoder_1_zy));
  assign not_1_out = ~X;  // NOT_Gate not_1, 16 bits wide
  assign not_2_out = ~Y;  // NOT_Gate not_2, 16 bits wide
  assign and_1_out = X & Y;  // AND_Gate and_1, 16 bits wide
  assign or_1_out = X | Y;  // OR_Gate or_1, 16 bits wide
  complement X_COMPLEMENT (.x(X), .nx(alu_decoder_1_nx), .neg_out(X_COMPLEMENT_neg_out));
  complement Y_COMPLEMENT (.x(Y), .nx(alu_decoder_1_ny), .neg_out(Y_COMPLEMENT_neg_out));
  assign not_3_out = ~16'h1;  // NOT_Gate not_3, 16 bits wide
  Adder #(.width(16)) adder_1 (.a(not_3_out), .b({16{1'b0}}), .out(adder_1_out), .cin(1'b1));  // open: cout
  zero ZERO_X (.x(X_COMPLEMENT_neg_out), .zx(alu_decoder_1_zx), .zero_out(ZERO_X_zero_out));
  zero ZERO_Y (.x(Y_COMPLEMENT_neg_out), .zx(alu_decoder_1_zy), .zero_out(ZERO_Y_zero_out));
  Multiplexer #(.select(3), .width(16)) multiplexer_1 (
    .in0(not_1_out), .in1(not_2_out), .in2(and_1_out), .in3(or_1_out), .in4({16{1'b0}}), .in5(16'h1),
    .in6(adder_1_out), .out(multiplexer_1_out), .sel(ALU_OP_CODE[2:0]));  // open: in7
  Adder #(.width(16)) adder_2 (
    .a(ZERO_X_zero_out), .b(ZERO_Y_zero_out), .out(adder_2_out), .cin(carry_in));  // open: cout
  Multiplexer #(.width(16)) multiplexer_2 (
    .in0(adder_2_out), .in1(multiplexer_1_out), .out(ALU_OUTPUT), .sel(ALU_OP_CODE[3]));
  nor nor_1 (Z_FLAG, ALU_OUTPUT[0], ALU_OUTPUT[1], ALU_OUTPUT[2], ALU_OUTPUT[3], ALU_OUTPUT[4], ALU_OUTPUT[5], ALU_OUTPUT[6], ALU_OUTPUT[7], ALU_OUTPUT[8], ALU_OUTPUT[9], ALU_OUTPUT[10], ALU_OUTPUT[11], ALU_OUTPUT[12], ALU_OUTPUT[13], ALU_OUTPUT[14], ALU_OUTPUT[15]);

  assign N_FLAG = ALU_OUTPUT[15];

  // Other names for the same wires on the sheet: OP_CODE[2:0] = ALU_OP_CODE[2:0]; F_CD = ALU_OP_CODE[3];
  //   X_OPERAND[15:0] = X; Y_OPERAND[15:0] = Y

  // Notes on the sheet:
  //   ARITHMETIC OPERATIONS
  //   LOGICAL OPERATIONS
  //   FLAG GENERATOR
endmodule

module CPU (
  input  [23:0] INSTRC,
  input  CLK,
  input  [15:0] VRAM_IN,
  input  [15:0] RAM_IN,
  input  RESET,
  output [15:0] OUT_BUS,
  output RAM_LOAD,
  output VRAM_LOAD,
  output [15:0] NXT_INSTRC,
  output [15:0] ADDR_RAM,
  output [15:0] ADDR_VRAM
);

  wire alu_1_n_flag, alu_1_z_flag, control_unit_1_alu_buffer, LOAD_IMM, n_flag_cell_out, prc_1_load,
       z_flag_cell_out;
  wire [1:0] JMP_CD;
  wire [2:0] DST_CD, ORIGIN_CD, X_OP_CD, Y_OP_CD;
  wire [3:0] ALU_OP;
  wire [15:0] alu_out, cpu_memory_unit_1_l_reg1_out, cpu_memory_unit_1_l_reg2_out, INSTRC_LN,
       multiplexer_1_out, multiplexer_2_out, VALUE;

  Control_Unit control_unit_1 (
    .INSTRUCTION(INSTRC), .LOAD_IMM(LOAD_IMM), .ORGIN_CD(ORIGIN_CD), .DST_CD(DST_CD), .VALUE(VALUE),
    .ALU_OP_CD(ALU_OP), .Y_OP_CD(Y_OP_CD), .X_OP_CD(X_OP_CD), .INSTRC_LN(INSTRC_LN), .JMP_CD(JMP_CD),
    .alu_buffer(control_unit_1_alu_buffer));
  CPU_Memory_Unit cpu_memory_unit_1 (
    .CLK(CLK), .VALUE(VALUE), .ORIGIN_REG_CODE(ORIGIN_CD), .LOAD_IMM(LOAD_IMM), .RAM_IN(RAM_IN),
    .DEST_REG_CODE(DST_CD), .VRAM_IN(VRAM_IN), .ALU_OUT(alu_out), .L_REG1_OUT(cpu_memory_unit_1_l_reg1_out),
    .L_REG2_OUT(cpu_memory_unit_1_l_reg2_out), .ADDR2_OUT(ADDR_VRAM), .OUT_BUS(OUT_BUS),
    .ADDR01_OUT(ADDR_RAM), .LOAD_ViREG1(RAM_LOAD), .LOAD_ViREG2(VRAM_LOAD));
  Multiplexer #(.select(3), .width(16)) multiplexer_1 (
    .in0(cpu_memory_unit_1_l_reg1_out), .in1(cpu_memory_unit_1_l_reg2_out), .in2(ADDR_RAM), .in3(ADDR_VRAM),
    .in4(RAM_IN), .in5(VRAM_IN), .in6(alu_out), .out(multiplexer_1_out), .sel(X_OP_CD));  // open: in7
  Multiplexer #(.select(3), .width(16)) multiplexer_2 (
    .in0(cpu_memory_unit_1_l_reg1_out), .in1(cpu_memory_unit_1_l_reg2_out), .in2(ADDR_RAM), .in3(ADDR_VRAM),
    .in4(RAM_IN), .in5(VRAM_IN), .in6(alu_out), .out(multiplexer_2_out), .sel(Y_OP_CD));  // open: in7
  ALU alu_1 (
    .ALU_OP_CODE(ALU_OP), .X(multiplexer_1_out), .Y(multiplexer_2_out), .ALU_OUTPUT(alu_out),
    .Z_FLAG(alu_1_z_flag), .N_FLAG(alu_1_n_flag));
  PrC prc_1 (.JMP_CD(JMP_CD), .ALU_N_FLAG(n_flag_cell_out), .ALU_Z_FLAG(z_flag_cell_out), .LOAD(prc_1_load));
  binary_cell n_flag (.CELL_IN(alu_1_n_flag), .LOAD(control_unit_1_alu_buffer), .CLK(CLK), .CELL_OUT(n_flag_cell_out));
  binary_cell z_flag (.CELL_IN(alu_1_z_flag), .LOAD(control_unit_1_alu_buffer), .CLK(CLK), .CELL_OUT(z_flag_cell_out));
  Program_Counter program_counter_1 (
    .INSTRC_ADDR(INSTRC_LN), .CLK(CLK), .RESET(RESET), .LOAD(prc_1_load), .NXT_INSTRC(NXT_INSTRC));
endmodule

module PrC (
  input  [1:0] JMP_CD,
  input  ALU_N_FLAG,
  input  ALU_Z_FLAG,
  output LOAD
);

  wire and_1_out, and_2_out, demultiplexer_1_out0, demultiplexer_1_out1, demultiplexer_1_out2,
       demultiplexer_1_out3, not_1_out;

  Demultiplexer #(.select(2)) demultiplexer_1 (
    .out0(demultiplexer_1_out0), .out1(demultiplexer_1_out1), .out2(demultiplexer_1_out2),
    .out3(demultiplexer_1_out3), .in(1'b1), .sel(JMP_CD));
  and and_1 (and_1_out, ~ALU_Z_FLAG, demultiplexer_1_out2);  // AND_Gate
  not not_1 (not_1_out, demultiplexer_1_out0);
  and and_2 (and_2_out, ALU_N_FLAG, demultiplexer_1_out1);
  Multiplexer #(.select(2)) multiplexer_1 (
    .in0(not_1_out), .in1(and_2_out), .in2(and_1_out), .in3(demultiplexer_1_out3), .out(LOAD), .sel(JMP_CD));

  // Notes on the sheet:
  //   NO JMP
  //   JMP != ZERO
  //   JMP LESS THAN ZERO
endmodule

module Program_Counter (
  input  [15:0] INSTRC_ADDR,
  input  CLK,
  input  RESET,
  input  LOAD,
  output [15:0] NXT_INSTRC
);

  wire [15:0] adder_1_out, multiplexer_1_out, multiplexer_2_out, multiplexer_3_out;

  Adder #(.width(16)) adder_1 (.a(NXT_INSTRC), .b({16{1'b0}}), .out(adder_1_out), .cin(1'b1));  // open: cout
  Multiplexer #(.width(16)) multiplexer_1 (.in0(NXT_INSTRC), .in1(adder_1_out), .out(multiplexer_1_out), .sel(1'b1));
  Multiplexer #(.width(16)) multiplexer_2 (
    .in0(multiplexer_1_out), .in1(INSTRC_ADDR), .out(multiplexer_2_out), .sel(LOAD));
  Multiplexer #(.width(16)) multiplexer_3 (
    .in0(multiplexer_2_out), .in1({16{1'b0}}), .out(multiplexer_3_out), .sel(RESET));
  registrador registrador_1 (.CLK(CLK), .LOAD(1'b1), .IN16(multiplexer_3_out), .OUT16(NXT_INSTRC));
endmodule

module complement (
  input  [15:0] x,
  input  nx,
  output [15:0] neg_out
);

  wire [15:0] not_1_out;

  assign not_1_out = ~x;  // NOT_Gate not_1, 16 bits wide
  Multiplexer #(.width(16)) multiplexer_1 (.in0(x), .in1(not_1_out), .out(neg_out), .sel(nx));
endmodule

module zero (
  input  [15:0] x,
  input  zx,
  output [15:0] zero_out
);

  wire [15:0] and_1_out;

  assign and_1_out = x & {16{1'b0}};  // AND_Gate and_1, 16 bits wide
  Multiplexer #(.width(16)) multiplexer_1 (.in0(x), .in1(and_1_out), .out(zero_out), .sel(zx));
endmodule

module ALU_DECODER (
  input  [2:0] ALU_F,
  output carry_in,
  output nx,
  output ny,
  output zx,
  output zy
);

  wire and_1_out, and_2_out, and_3_out, and_4_out, and_5_out, and_6_out, and_7_out, and_8_out;

  and and_1 (and_1_out, ~ALU_F[0], ALU_F[1], ~ALU_F[2]);  // AND_Gate
  and and_2 (and_2_out, ALU_F[0], ALU_F[1], ~ALU_F[2]);  // AND_Gate
  and and_3 (and_3_out, ALU_F[0], ~ALU_F[1], ~ALU_F[2]);  // AND_Gate
  and and_4 (and_4_out, ~ALU_F[0], ~ALU_F[1], ALU_F[2]);  // AND_Gate
  and and_5 (and_5_out, ~ALU_F[0], ~ALU_F[1], ALU_F[2]);  // AND_Gate
  and and_6 (and_6_out, ~ALU_F[0], ALU_F[1], ALU_F[2]);  // AND_Gate
  and and_7 (and_7_out, ALU_F[0], ALU_F[1], ~ALU_F[2]);  // AND_Gate
  and and_8 (and_8_out, ALU_F[0], ~ALU_F[1], ALU_F[2]);  // AND_Gate
  or or_1 (carry_in, ALU_F[0], ALU_F[1], ALU_F[2]);
  or or_2 (nx, and_1_out, and_2_out);
  or or_3 (ny, and_3_out, and_4_out);
  or or_4 (zx, and_5_out, and_6_out);
  or or_5 (zy, and_7_out, and_8_out);
endmodule
